// Logisim project 系统控制器.circ as structural Verilog: 1 circuit, main circuit main
module main (
  input  C,
  input  B,
  input  A,
  input  U,
  input  V,
  input  W,
  input  X,
  input  Y,
  input  Z,
  output Cn_1,
  output Bn_1,
  output An_1
);

  wire and_1_out, and_3_out, and_4_out, and_5_out, and_6_out, and_7_out, and_8_out, and_9_out, and_10_out,
       not_1_out, not_2_out, not_3_out, not_4_out, not_5_out, not_6_out, not_7_out, not_8_out, not_9_out,
       not_10_out, not_11_out, not_12_out, not_13_out, not_14_out, not_15_out, not_16_out, not_17_out,
       not_18_out, not_19_out, not_20_out, not_21_out, not_22_out, not_23_out, not_24_out, or_1_out;

  not not_1 (not_1_out, C);
  not not_2 (not_2_out, B);
  not not_3 (not_3_out, W);
  not not_4 (not_4_out, X);
  not not_5 (not_5_out, C);
  not not_6 (not_6_out, B);
  not not_7 (not_7_out, W);
  not not_8 (not_8_out, B);
  not not_9 (not_9_out, A);
  not not_10 (not_10_out, C);
  not not_11 (not_11_out, A);
  not not_12 (not_12_out, Z);
  not not_13 (not_13_out, V);
  and and_1 (and_1_out, V, W);
  and and_2 (Cn_1, not_1_out, not_2_out, A, V, not_3_out, not_4_out);
  and and_3 (and_3_out, not_5_out, not_6_out, A, V, not_7_out, X);
  and and_4 (and_4_out, C, not_8_out, not_9_out, Y);
  and and_5 (and_5_out, not_10_out, B, not_11_out, not_12_out);
  not not_14 (not_14_out, C);
  not not_15 (not_15_out, B);
  not not_16 (not_16_out, A);
  not not_17 (not_17_out, C);
  not not_18 (not_18_out, B);
  or or_1 (or_1_out, not_13_out, and_1_out);
  not not_19 (not_19_out, C);
  not not_20 (not_20_out, B);
  not not_21 (not_21_out, W);
  not not_22 (not_22_out, C);
  not not_23 (not_23_out, C);
  not not_24 (not_24_out, A);
  or or_2 (Bn_1, and_3_out, and_4_out, and_5_out);
  and and_6 (and_6_out, not_14_out, not_15_out, not_16_out, U);
  and and_7 (and_7_out, not_17_out, not_18_out, A, or_1_out);
  and and_8 (and_8_out, not_19_out, not_20_out, A, V, not_21_out, X);
  and and_9 (and_9_out, not_22_out, B, A, Y);
  and and_10 (and_10_out, not_23_out, B, not_24_out, Z);
  or or_3 (An_1, and_6_out, and_7_out, and_8_out, and_9_out, and_10_out);
endmodule
